// Logisim project design.circ as structural Verilog: 9 circuits, main circuit main
module main (
  output [6:0] out_1,
  output [15:0] out_2
);

  wire AC_out, analizadorteclado_1_out_4, or_1_out, or_2_out;
  wire [6:0] analizadorteclado_1_salida_ascii;
  wire [18:0] _1_out;

  or or_1 (or_1_out, analizadorteclado_1_out_4, analizadorteclado_1_out_4);
  AnalizadorTeclado analizadorteclado_1 (
    .Entrada(_1_out), .Salida_ASCII(analizadorteclado_1_salida_ascii), .Salida_binario(out_1),
    .out_4(analizadorteclado_1_out_4));
  TTY #(.rows(1), .cols(30)) tty_1 (
    .data(analizadorteclado_1_salida_ascii), .clk(analizadorteclado_1_out_4), .clr(or_2_out));  // open: we
  or or_2 (or_2_out, _1_out[10], AC_out);
  Button _1 (.out(_1_out[0]));
  Button _2 (.out(_1_out[1]));
  Button _5 (.out(_1_out[4]));
  Button _4 (.out(_1_out[3]));
  Button _7 (.out(_1_out[6]));
  Button _8 (.out(_1_out[7]));
  Button AC (.out(AC_out));
  Button _0 (.out(_1_out[9]));
  MemoriaInstrucciones memoriainstrucciones_1 (
    .Entrada(out_1), .Reloj(or_1_out), .Reset_mem(AC_out), ._0_leer_1_escribir(_1_out[10]),
    .Procesar(out_2[0]));
  Button _3 (.out(_1_out[2]));
  Button _6 (.out(_1_out[5]));
  Button _9 (.out(_1_out[8]));
  Button button (.out(_1_out[10]));
  Button button_2 (.out(_1_out[18]));
  Button button_3 (.out(_1_out[14]));
  Button button_4 (.out(_1_out[13]));
  Button button_5 (.out(_1_out[17]));
  Button button_6 (.out(_1_out[16]));
  Button x (.out(_1_out[12]));
  Button button_7 (.out(_1_out[11]));
  Button x_y (.out(_1_out[15]));
  // Pins of 1 and 16 bits meet at out_2
endmodule

module MemoriaInstrucciones (
  input  [6:0] Entrada,
  input  Reloj,
  input  Reset_mem,
  input  _0_leer_1_escribir,
  output Procesar
);

  wire alu_1_terminado, and_1_out, and_2_out, and_3_out, and_4_out, and_5_out, and_6_out, clock_1_out,
       comparator_2_eq, comparator_3_lt, ne, not_1_out, not_2_out, not_4_out, not_5_out, not_6_out, or_1_out,
       or_2_out, si_soy_un_operador_out_2, t_ff_1_qn, tunnel;
  wire [3:0] ram_2_data;
  wire [6:0] adder_1_out, bit_extender_1_out, counter_1_q, register_1_q;
  wire [7:0] counter_2_q;
  wire [15:0] alu_1_out_4, controlled_buffer_2_out, controlled_buffer_3_out, controlled_buffer_4_out,
       controlled_buffer_5_out, controlled_buffer_6_out, decodificadordeinstrucciones_1_salida,
       multiplexer_2_out, ram_1_data, register_2_q, register_3_q;
  wire [19:0] multiplexer_1_out;
  wire [19:4] ram_2_data_2;

  Register #(.width(7), .Select("low")) register_1 (
    .D(Entrada), .Q(register_1_q), .clk(Reloj), .clr(Reset_mem));  // open: en
  Counter #(.width(7), .max('h7f)) counter_1 (
    .Q(counter_1_q), .clk(tunnel), .clr(or_1_out));  // open: load, D, count, carry, preset, down
  or or_1 (or_1_out, _0_leer_1_escribir, Reset_mem);
  decodificadorDeInstrucciones decodificadordeinstrucciones_1 (
    .Reloj(Reloj), .Entrada(register_1_q), .Reset(Reset_mem), .Salida(decodificadordeinstrucciones_1_salida));
  Comparator #(.width(7)) comparator_1 (.a(register_1_q), .b(7'b0100000), .eq(tunnel));  // open: gt, lt
  RAM #(.addrWidth(7), .dataWidth(16), .Select("high")) ram_1 (
    .addr(counter_1_q), .data(ram_1_data), .clk(Reloj), .ld(Procesar), .clr(Reset_mem));  // open: sel
  T_Flip_Flop t_ff_1 (
    .clk(_0_leer_1_escribir), .T(1'b1), .Q(Procesar), .Qn(t_ff_1_qn), .reset(Reset_mem));  // open: preset
  not not_1 (not_1_out, tunnel);
  and and_1 (and_1_out, not_1_out, t_ff_1_qn);
  assign ram_1_data = and_1_out ? decodificadordeinstrucciones_1_salida : 16'bz;  // Controlled_Buffer controlled_buffer_1
  assign controlled_buffer_2_out = Procesar ? ram_1_data : 16'bz;  // Controlled_Buffer controlled_buffer_2
  EsCodigoOperacion si_soy_un_operador (.in_1(ram_1_data), .out_2(si_soy_un_operador_out_2));
  not not_2 (not_2_out, si_soy_un_operador_out_2);
  assign controlled_buffer_3_out = not_2_out ? ram_1_data : 16'bz;  // Controlled_Buffer controlled_buffer_3
  not not_3 (ne, si_soy_un_operador_out_2);
  assign controlled_buffer_4_out = si_soy_un_operador_out_2 ? ram_1_data : 16'bz;  // Controlled_Buffer controlled_buffer_4
  or or_2 (or_2_out, si_soy_un_operador_out_2, not_2_out);
  Bit_Extender #(.out_width(7), .\type ("zero")) bit_extender_1 (.in(counter_2_q), .out(bit_extender_1_out));
  Multiplexer #(.width(20), .enable("false")) multiplexer_1 (
    .in0({4'b0000, controlled_buffer_4_out}), .in1({controlled_buffer_3_out, 4'b0011}),
    .out(multiplexer_1_out), .sel(ne));
  and and_2 (and_2_out, or_2_out, Reloj);
  Adder #(.width(7)) adder_1 (.a(counter_1_q), .b(bit_extender_1_out), .out(adder_1_out));  // open: cin, cout
  RAM #(.addrWidth(7), .dataWidth(20), .bus("separate"), .Select("low")) ram_2 (
    .addr(adder_1_out), .din(multiplexer_1_out), .data({ram_2_data_2, ram_2_data}), .clk(and_2_out),
    .clr(1'b0));  // open: str, sel, ld
  Comparator #(.width(4)) comparator_2 (.a(ram_2_data), .b(4'b0011), .eq(comparator_2_eq));  // open: gt, lt
  assign controlled_buffer_5_out = and_3_out ? ram_2_data_2 : 16'bz;  // Controlled_Buffer controlled_buffer_5
  and and_3 (and_3_out, comparator_3_lt, comparator_2_eq);
  not not_4 (not_4_out, comparator_3_lt);
  and and_4 (and_4_out, comparator_2_eq, not_4_out);
  assign controlled_buffer_6_out = and_4_out ? ram_2_data_2 : 16'bz;  // Controlled_Buffer controlled_buffer_6
  Multiplexer #(.width(16), .enable("false")) multiplexer_2 (
    .in0(controlled_buffer_5_out), .in1(alu_1_out_4), .out(multiplexer_2_out), .sel(not_5_out));
  not not_5 (not_5_out, comparator_3_lt);
  Clock clock_1 (.out(clock_1_out));
  Counter counter_2 (
    .count(alu_1_terminado), .Q(counter_2_q), .clk(and_5_out));  // open: load, D, carry, clr, preset, down
  Register #(.width(16), .trigger("falling"), .Select("low")) register_2 (
    .D(multiplexer_2_out), .Q(register_2_q), .clk(and_5_out), .cs(alu_1_terminado));  // open: en, clr, preset
  Register #(.width(16), .Select("low")) register_3 (
    .D(controlled_buffer_6_out), .Q(register_3_q), .clk(and_6_out));  // open: en, clr
  not not_6 (not_6_out, comparator_3_lt);
  and and_5 (and_5_out, clock_1_out, Procesar);
  Comparator comparator_3 (.a(counter_2_q), .b(8'h1), .lt(comparator_3_lt));  // open: gt, eq
  and and_6 (and_6_out, and_5_out, not_6_out);
  ALU alu_1 (
    .Operando_1(register_2_q), .Operando_2(register_3_q), .out_4(alu_1_out_4), .Operador(ram_2_data),
    .terminado(alu_1_terminado));

  // Notes on the sheet:
  //   CODIGO OPERACION
  //   Dato
endmodule

module AnalizadorTeclado (
  input  [18:0] Entrada,
  output [6:0] Salida_ASCII,
  output [6:0] Salida_binario,
  output out_4
);

  Register #(.width(19), .Select("low")) register_1 (.D(Entrada), .clk(out_4));  // open: en, Q, clr
  ROM #(.addrWidth(19), .dataWidth(7), .Select("low")) rom_1 (.addr(Entrada), .data(Salida_ASCII));
  ROM #(.addrWidth(19), .dataWidth(7), .Select("low")) rom_2 (.addr(Entrada), .data(Salida_binario));
  or or_1 (out_4, Salida_ASCII[0], Salida_ASCII[1], Salida_ASCII[2], Salida_ASCII[3], Salida_ASCII[4], Salida_ASCII[5], Salida_ASCII[6]);

  // Notes on the sheet:
  //   contents of rom_1 (hex, n*v repeats v):
  //   0 31 32 0 33 0 0 0 34 7*0 35 15*0 36 31*0 37 63*0 38 127*0 39 255*0 30 511*0 3d 1023*0 21 2047*0 2a
  //   4095*0 2b 8191*0 20 16383*0 5e 32767*0 2f 65535*0 2d 131071*0 25
  //   contents of rom_2 (hex, n*v repeats v):
  //   0 1 2 0 3 0 0 0 4 7*0 5 15*0 6 31*0 7 63*0 8 127*0 9 767*0 3d 1023*0 21 2047*0 2a 4095*0 2b 8191*0
  //   20 16383*0 5e 32767*0 2f 65535*0 2d 131071*0 25
endmodule

module Potenciador (
  input  [15:0] Base,
  input  [15:0] Exponente,
  input  Reloj,
  output [15:0] Salida,
  output terminado
);

  wire comparator_1_eq, comparator_2_eq, not_1_out, register_3_q;
  wire [15:0] counter_1_q, multiplexer_1_out, multiplier_1_out, register_1_q, register_2_q;

  Multiplexer #(.width(16), .enable("false")) multiplexer_1 (
    .in0(Base), .in1(multiplier_1_out), .out(multiplexer_1_out), .sel(not_1_out));
  not not_1 (not_1_out, comparator_2_eq);
  Register #(.width(16), .Select("low")) register_1 (.D(Exponente), .Q(register_1_q), .clk(Reloj));  // open: en, clr
  Counter #(.width(16), .max('hffff)) counter_1 (
    .Q(counter_1_q), .clk(Reloj), .clr(register_3_q));  // open: load, D, count, carry, preset, down
  Register #(.width(16), .Select("low")) register_2 (
    .D(multiplexer_1_out), .Q(register_2_q), .clk(Reloj));  // open: en, clr
  Comparator #(.width(16)) comparator_1 (.a(register_1_q), .b(counter_1_q), .eq(comparator_1_eq));  // open: gt, lt
  Comparator #(.width(16)) comparator_2 (.a(counter_1_q), .b({16{1'b0}}), .eq(comparator_2_eq));  // open: gt, lt
  Multiplier #(.width(16)) multiplier_1 (.a(register_2_q), .b(Base), .out(multiplier_1_out));  // open: cin, cout
  Register #(.width(1), .Select("low")) register_3 (
    .D(comparator_1_eq), .Q(register_3_q), .clk(Reloj));  // open: en, clr
  Comparator #(.width(1)) comparator_3 (.a(register_3_q), .b(1'b1), .eq(terminado));  // open: gt, lt
  Register #(.width(16), .Select("low")) register_4 (
    .D(register_2_q), .en(comparator_1_eq), .Q(Salida), .clk(Reloj));  // open: clr

  // Notes on the sheet:
  //   Contador
endmodule

module Factorial (
  input  [15:0] Number,
  input  in_2,
  input  in_3,
  output [15:0] out_4
);

  wire comparator_1_eq, comparator_2_eq, comparator_2_gt, not_1_out, or_1_out;
  wire [15:0] counter_1_q, multiplexer_1_out, multiplier_1_out, register_1_q, register_2_q, register_4_q,
       subtractor_1_out;

  Multiplexer #(.width(16), .enable("false")) multiplexer_1 (
    .in0(multiplier_1_out), .in1(Number), .out(multiplexer_1_out), .sel(comparator_1_eq));
  Register #(.width(16), .Select("low")) register_1 (
    .D(multiplexer_1_out), .Q(register_1_q), .clk(in_2), .clr(in_3));  // open: en
  Counter #(.width(16), .max('hffff)) counter_1 (
    .Q(counter_1_q), .clk(in_2), .clr(in_3));  // open: load, D, count, carry, preset, down
  Register #(.width(16), .Select("low")) register_2 (.Q(register_2_q));  // open: D, en, clk, clr
  not not_1 (not_1_out, or_1_out);
  Subtractor #(.width(16)) subtractor_1 (.a(register_4_q), .b(counter_1_q), .out(subtractor_1_out));  // open: bin, bout
  Comparator #(.width(16)) comparator_1 (.a(counter_1_q), .b(register_2_q), .eq(comparator_1_eq));  // open: gt, lt
  or or_1 (or_1_out, comparator_2_gt, comparator_2_eq);
  Register #(.width(16), .Select("low")) register_3 (
    .D(multiplier_1_out), .en(not_1_out), .Q(out_4), .clk(in_2), .clr(in_3));
  Multiplier #(.width(16)) multiplier_1 (
    .a(register_1_q), .b(subtractor_1_out), .out(multiplier_1_out));  // open: cin, cout
  Comparator #(.width(16)) comparator_2 (
    .a(counter_1_q), .b(register_4_q), .gt(comparator_2_gt), .eq(comparator_2_eq));  // open: lt
  Register #(.width(16), .Select("low")) register_4 (
    .D(Number), .en(comparator_1_eq), .Q(register_4_q), .clk(in_2), .clr(in_3));
endmodule

module decodificadorDeInstrucciones (
  input  Reloj,
  input  [6:0] Entrada,
  input  Reset,
  output [15:0] Salida
);

  wire comparator_1_gt, comparator_1_lt, comparator_2_eq, d_ff_1_qn, nand_1_out, or_1_out;
  wire [15:0] bit_extender_1_out, multiplexer_1_out, multiplier_1_out, register_1_q;

  D_Flip_Flop d_ff_1 (.clk(Reloj), .D(comparator_1_gt), .Qn(d_ff_1_qn));  // open: Q, preset, reset
  Comparator #(.width(7)) comparator_1 (
    .a(Entrada), .b(7'b0001010), .gt(comparator_1_gt), .lt(comparator_1_lt));  // open: eq
  Comparator #(.width(7)) comparator_2 (.a(Entrada), .b(7'b0100000), .eq(comparator_2_eq));  // open: gt, lt
  assign bit_extender_1_out = {{9{1'b0}}, Entrada};  // Bit_Extender bit_extender_1
  nand nand_1 (nand_1_out, d_ff_1_qn, comparator_1_lt);
  or or_1 (or_1_out, comparator_2_eq, Reset);
  Register #(.width(16), .Select("low")) register_1 (
    .D(Salida), .Q(register_1_q), .clk(Reloj), .clr(or_1_out));  // open: en
  Multiplier #(.width(16)) multiplier_1 (.a(register_1_q), .b(16'ha), .out(multiplier_1_out));  // open: cin, cout
  Multiplexer #(.width(16), .enable("false")) multiplexer_1 (
    .in0(multiplier_1_out), .in1({16{1'b0}}), .out(multiplexer_1_out), .sel(nand_1_out));
  Adder #(.width(16)) adder_1 (.a(multiplexer_1_out), .b(bit_extender_1_out), .out(Salida));  // open: cin, cout

  // Notes on the sheet:
  //   Estados:
  //   0- Número
  //   1- Operador
endmodule

module ALU (
  input  [15:0] Operando_1,
  input  [15:0] Operando_2,
  input  [3:0] Operador,
  output [15:0] out_4,
  output terminado
);

  wire clock_1_out, potenciador_1_terminado;
  wire [15:0] adder_1_out, divider_1_out, factorial_1_out_4, multiplier_1_out, potenciador_1_salida,
       subtractor_1_out;

  Clock clock_1 (.out(clock_1_out));
  Adder #(.width(16)) adder_1 (.a(Operando_1), .b(Operando_1), .out(adder_1_out));  // open: cin, cout
  Subtractor #(.width(16)) subtractor_1 (.a(Operando_1), .b(Operando_1), .out(subtractor_1_out));  // open: bin, bout
  Multiplier #(.width(16)) multiplier_1 (.a(Operando_1), .b(Operando_1), .out(multiplier_1_out));  // open: cin, cout
  Divider #(.width(16)) divider_1 (.a(Operando_1), .b(Operando_1), .out(divider_1_out));  // open: upper, rem
  Factorial factorial_1 (.Number(Operando_1), .in_2(clock_1_out), .out_4(factorial_1_out_4));  // open: in_3
  Potenciador potenciador_1 (
    .Base(Operando_1), .Exponente(Operando_1), .Reloj(clock_1_out), .Salida(potenciador_1_salida),
    .terminado(potenciador_1_terminado));
  Multiplexer #(.select(4), .width(16), .enable("false")) multiplexer_1 (
    .in1(factorial_1_out_4), .in10(multiplier_1_out), .in11(adder_1_out), .in13(subtractor_1_out),
    .in14(potenciador_1_salida), .in15(divider_1_out), .out(out_4), .sel(Operador));  // open: in0, in2, in3, in4, in5, in6, in7, in8, in9, in12
  or or_1 (terminado, 1'b0, potenciador_1_terminado);

  assign Operando_2 = Operando_1;

  // Notes on the sheet:
  //   1011 SUMA
  //   1101 RESTA
  //   1111 Division
  //   0001 Factorial
  //   1010 Multiplicacion
  //   1110 Exponente
endmodule

module Convertidor7bitAsciiA4bits (
  input  [15:0] in_1,
  output [3:0] out_2
);


  assign out_2 = in_1[3:0];

  // Notes on the sheet:
  //   1011 SUMA
  //   1101 RESTA
  //   1010 Multiplicacion
  //   1111 Division
  //   1110 Exponente
  //   0001 Factorial
endmodule

module EsCodigoOperacion (
  input  [15:0] in_1,
  output out_2
);

  wire comparator_1_eq, comparator_2_eq, comparator_3_eq, comparator_4_eq, comparator_5_eq, comparator_6_eq;

  Comparator #(.width(16)) comparator_1 (.a(in_1), .b(16'h2b), .eq(comparator_1_eq));  // open: gt, lt
  Comparator #(.width(16)) comparator_2 (.a(in_1), .b(16'h2d), .eq(comparator_2_eq));  // open: gt, lt
  Comparator #(.width(16)) comparator_3 (.a(in_1), .b(16'h2a), .eq(comparator_3_eq));  // open: gt, lt
  Comparator #(.width(16)) comparator_4 (.a(in_1), .b(16'h2f), .eq(comparator_4_eq));  // open: gt, lt
  Comparator #(.width(16)) comparator_5 (.a(in_1), .b(16'h21), .eq(comparator_5_eq));  // open: gt, lt
  Comparator #(.width(16)) comparator_6 (.a(in_1), .b(16'h5e), .eq(comparator_6_eq));  // open: gt, lt
  or or_1 (out_2, comparator_1_eq, comparator_2_eq, comparator_3_eq, comparator_4_eq, comparator_5_eq, comparator_6_eq);
endmodule
